// Logisim project Simplified Processor Module_Team Number 13.circ as structural Verilog: 28 circuits, main circuit main
module main (
  input  RESET
);

  wire CLK_out;
  wire [7:0] counter_1_q, processor_1_output;
  wire [15:0] rom_1_data;

  Counter counter_1 (.Q(counter_1_q), .clk(CLK_out), .clr(RESET));  // open: load, D, count, carry
  Clock CLK (.out(CLK_out));
  ROM #(.dataWidth(16)) rom_1 (.addr(counter_1_q), .data(rom_1_data));  // open: sel
  Processor processor_1 (.instruction(rom_1_data), .CLK(CLK_out), .RESET(RESET), .OUTPUT(processor_1_output));
  Hex_Digit_Display hex_digit_display_1 (.value(processor_1_output[7:4]));  // open: dp
  Hex_Digit_Display hex_digit_display_2 (.value(processor_1_output[3:0]));  // open: dp

  // Notes on the sheet:
  //   contents of rom_1 (hex, n*v repeats v):
  //   135 800 200 8bf0 ab04 400 8d0f a504 9202 a00 600 8e01 e00 600 9601 e00 600 9e01 e00 600 8600 e00 601
  //   8600 e00
endmodule

module Processor (
  input  CLK,
  input  RESET,
  input  [15:0] instruction,
  output [7:0] OUTPUT
);

  wire cunit_1_enwr, cunit_1_scren;
  wire [1:0] cunit_1_desadd, cunit_1_scradd;
  wire [4:0] cunit_1_op;
  wire [7:0] alu_1_result, cunit_1_op1, cunit_1_op2, cunit_1_retost, regfile_1_destop, regfile_1_scrop;

  Cunit cunit_1 (
    .Scr(regfile_1_scrop), .instruction(instruction), .Dest(regfile_1_destop), .Result(alu_1_result),
    .OP(cunit_1_op), .Scradd(cunit_1_scradd), .Op1(cunit_1_op1), .ScrEn(cunit_1_scren),
    .DesAdd(cunit_1_desadd), .EnWr(cunit_1_enwr), .Op2(cunit_1_op2), .ReToSt(cunit_1_retost));
  ALU alu_1 (.Dest(cunit_1_op2), .Src(cunit_1_op1), .OP(cunit_1_op), .Result(alu_1_result));
  RegFile regfile_1 (
    .NewData(cunit_1_retost), .CLK(CLK), .RESET(RESET), .ScrE(cunit_1_scren), .ScrAdd(cunit_1_scradd),
    .DestAdd(cunit_1_desadd), .ScrOP(regfile_1_scrop), .DestOP(regfile_1_destop));
  Reg8bit reg8bit_1 (.Dest(cunit_1_retost), .CLK(CLK), .RESET(RESET), .EnWr(cunit_1_enwr), .Out(OUTPUT));
endmodule

module Cunit (
  input  [7:0] Scr,
  input  [15:0] instruction,
  input  [7:0] Dest,
  input  [7:0] Result,
  output [1:0] Scradd,
  output [7:0] Op1,
  output ScrEn,
  output [1:0] DesAdd,
  output EnWr,
  output [7:0] Op2,
  output [4:0] OP,
  output [7:0] ReToSt
);

  wire not_1_out, not_2_out, not_3_out, not_4_out;

  not not_1 (not_1_out, instruction[12]);
  not not_2 (not_2_out, instruction[13]);
  not not_3 (not_3_out, instruction[14]);
  not not_4 (not_4_out, instruction[15]);
  and and_1 (EnWr, instruction[11], not_1_out, not_2_out, not_3_out, not_4_out);
  _2_1Mux_8bits u_2_1mux_8bits_1 (.D0(Scr), .D1(instruction[7:0]), .S0(instruction[8]), .En(1'b1), .Y(Op1));
  not not_5 (ScrEn, instruction[8]);

  assign DesAdd = instruction[10:9];
  assign OP = instruction[15:11];
  assign Op2 = Dest;
  assign ReToSt = Result;
  assign Scradd = instruction[1:0];
endmodule

module RegFile (
  input  [7:0] NewData,
  input  CLK,
  input  RESET,
  input  [1:0] ScrAdd,
  input  [1:0] DestAdd,
  input  ScrE,
  output [7:0] ScrOP,
  output [7:0] DestOP
);

  wire n2_4dec_1_d0, n2_4dec_1_d1, n2_4dec_1_d2, n2_4dec_1_d3;
  wire [7:0] reg8bit_1_out, reg8bit_2_out, reg8bit_3_out, reg8bit_4_out;

  Reg8bit reg8bit_1 (.Dest(NewData), .CLK(CLK), .RESET(RESET), .EnWr(n2_4dec_1_d0), .Out(reg8bit_1_out));
  Reg8bit reg8bit_2 (.Dest(NewData), .CLK(CLK), .RESET(RESET), .EnWr(n2_4dec_1_d1), .Out(reg8bit_2_out));
  Reg8bit reg8bit_3 (.Dest(NewData), .CLK(CLK), .RESET(RESET), .EnWr(n2_4dec_1_d2), .Out(reg8bit_3_out));
  Reg8bit reg8bit_4 (.Dest(NewData), .CLK(CLK), .RESET(RESET), .EnWr(n2_4dec_1_d3), .Out(reg8bit_4_out));
  _2_4Dec u_2_4dec_1 (.in_1(DestAdd), .D0(n2_4dec_1_d0), .D1(n2_4dec_1_d1), .D2(n2_4dec_1_d2), .D3(n2_4dec_1_d3));
  _4_1Mux u_4_1mux_1 (
    .D0(reg8bit_1_out), .D1(reg8bit_2_out), .D2(reg8bit_3_out), .D3(reg8bit_4_out), .En(ScrE), .S(ScrAdd),
    .Y(ScrOP));
  _4_1Mux u_4_1mux_2 (
    .D0(reg8bit_1_out), .D1(reg8bit_2_out), .D2(reg8bit_3_out), .D3(reg8bit_4_out), .En(1'b1), .S(DestAdd),
    .Y(DestOP));
endmodule

module Reg8bit (
  input  [7:0] Dest,
  input  EnWr,
  input  CLK,
  input  RESET,
  output [7:0] Out
);

  wire n2_1mux_1bit_1_y, n2_1mux_1bit_2_y, n2_1mux_1bit_3_y, n2_1mux_1bit_4_y, n2_1mux_1bit_5_y,
       n2_1mux_1bit_6_y, n2_1mux_1bit_7_y, n2_1mux_1bit_8_y;

  _2_1Mux_1bit u_2_1mux_1bit_1 (.S0(EnWr), .D0(Out[7]), .D1(Dest[7]), .En(1'b1), .Y(n2_1mux_1bit_1_y));
  D_Flip_Flop d_ff_1 (.clk(CLK), .D(n2_1mux_1bit_1_y), .Q(Out[7]), .en(EnWr), .reset(RESET));  // open: Qn, preset
  _2_1Mux_1bit u_2_1mux_1bit_2 (.S0(EnWr), .D0(Out[6]), .D1(Dest[6]), .En(1'b1), .Y(n2_1mux_1bit_2_y));
  D_Flip_Flop d_ff_2 (.clk(CLK), .D(n2_1mux_1bit_2_y), .Q(Out[6]), .en(EnWr), .reset(RESET));  // open: Qn, preset
  _2_1Mux_1bit u_2_1mux_1bit_3 (.S0(EnWr), .D0(Out[5]), .D1(Dest[5]), .En(1'b1), .Y(n2_1mux_1bit_3_y));
  D_Flip_Flop d_ff_3 (.clk(CLK), .D(n2_1mux_1bit_3_y), .Q(Out[5]), .en(EnWr), .reset(RESET));  // open: Qn, preset
  _2_1Mux_1bit u_2_1mux_1bit_4 (.S0(EnWr), .D0(Out[4]), .D1(Dest[4]), .En(1'b1), .Y(n2_1mux_1bit_4_y));
  D_Flip_Flop d_ff_4 (.clk(CLK), .D(n2_1mux_1bit_4_y), .Q(Out[4]), .en(EnWr), .reset(RESET));  // open: Qn, preset
  _2_1Mux_1bit u_2_1mux_1bit_5 (.S0(EnWr), .D0(Out[3]), .D1(Dest[3]), .En(1'b1), .Y(n2_1mux_1bit_5_y));
  _2_1Mux_1bit u_2_1mux_1bit_6 (.S0(EnWr), .D0(Out[2]), .D1(Dest[2]), .En(1'b1), .Y(n2_1mux_1bit_6_y));
  D_Flip_Flop d_ff_5 (.clk(CLK), .D(n2_1mux_1bit_5_y), .Q(Out[3]), .en(EnWr), .reset(RESET));  // open: Qn, preset
  _2_1Mux_1bit u_2_1mux_1bit_7 (.S0(EnWr), .D0(Out[1]), .D1(Dest[1]), .En(1'b1), .Y(n2_1mux_1bit_7_y));
  D_Flip_Flop d_ff_6 (.clk(CLK), .D(n2_1mux_1bit_6_y), .Q(Out[2]), .en(EnWr), .reset(RESET));  // open: Qn, preset
  D_Flip_Flop d_ff_7 (.clk(CLK), .D(n2_1mux_1bit_7_y), .Q(Out[1]), .en(EnWr), .reset(RESET));  // open: Qn, preset
  _2_1Mux_1bit u_2_1mux_1bit_8 (.S0(EnWr), .D0(Out[0]), .D1(Dest[0]), .En(1'b1), .Y(n2_1mux_1bit_8_y));
  D_Flip_Flop d_ff_8 (.clk(CLK), .D(n2_1mux_1bit_8_y), .Q(Out[0]), .en(EnWr), .reset(RESET));  // open: Qn, preset
endmodule

module ALU (
  input  [7:0] Dest,
  input  [7:0] Src,
  input  [4:0] OP,
  output [7:0] Result
);

  wire and_2_out, not_2_out, not_3_out, not_4_out;
  wire [7:0] a_s_1_out_19, and_1_out_3, imult_1_out_3, mult_1_out_3, neg_1_out_2, not_1_out_2, or_1_out_3,
       shl_1_out_3, shr_1_out_3, xor_1_out_3;

  NOT not_1 (.Dest(Dest), .out_2(not_1_out_2));
  AND and_1 (.Dest(Dest), .Src(Src), .out_3(and_1_out_3));
  OR or_1 (.Dest(Dest), .Src(Src), .out_3(or_1_out_3));
  XOR xor_1 (.Dest(Dest), .Src(Src), .out_3(xor_1_out_3));
  SHL shl_1 (.Dest(Dest), .Src(Src), .out_3(shl_1_out_3));
  Mult mult_1 (.Dest(Dest), .Src(Src), .out_3(mult_1_out_3));
  IMult imult_1 (.Dest(Dest), .Src(Src), .out_3(imult_1_out_3));
  SHR shr_1 (.Dest(Dest), .Src(Src), .out_3(shr_1_out_3));
  A_S a_s_1 (
    .Sel(and_2_out), .X0(Dest[0]), .X2(Dest[2]), .X3(Dest[3]), .X1(Dest[1]), .Y2(Src[2]), .Y3(Src[3]),
    .Y0(Src[0]), .Y1(Src[1]), .X7(Dest[7]), .X5(Dest[5]), .X6(Dest[6]), .X4(Dest[4]), .Y7(Src[7]),
    .Y5(Src[5]), .Y6(Src[6]), .Y4(Src[4]), .out_19(a_s_1_out_19));  // open: FC
  and and_2 (and_2_out, OP[0], not_2_out, not_3_out, OP[3], not_4_out);
  Neg neg_1 (.Dest(Dest), .out_2(neg_1_out_2));
  not not_2 (not_2_out, OP[1]);
  not not_3 (not_3_out, OP[2]);
  not not_4 (not_4_out, OP[4]);
  _32_1Mux u_32_1mux_1 (
    .D0(Src), .D1(Dest), .D2({8{1'b0}}), .D3({8{1'b0}}), .D4({8{1'b0}}), .D5({8{1'b0}}), .D6({8{1'b0}}),
    .D7({8{1'b0}}), .D8(a_s_1_out_19), .D9(a_s_1_out_19), .D10(neg_1_out_2), .D11({8{1'b0}}),
    .D12(mult_1_out_3), .D13(imult_1_out_3), .D14({8{1'b0}}), .D15({8{1'b0}}), .S(OP), .D16(not_1_out_2),
    .D17(and_1_out_3), .D18(or_1_out_3), .D19(xor_1_out_3), .D20(shl_1_out_3), .D21(shr_1_out_3),
    .D22({8{1'b0}}), .D23({8{1'b0}}), .D24({8{1'b0}}), .D25({8{1'b0}}), .D26({8{1'b0}}), .D27({8{1'b0}}),
    .D28({8{1'b0}}), .D29({8{1'b0}}), .D30({8{1'b0}}), .D31({8{1'b0}}), .Y(Result));
endmodule

module A_S (
  input  Sel,
  input  X0,
  input  X2,
  input  X3,
  input  X1,
  input  Y2,
  input  Y3,
  input  Y0,
  input  Y1,
  input  X7,
  input  X5,
  input  X6,
  input  X4,
  input  Y7,
  input  Y5,
  input  Y6,
  input  Y4,
  output FC,
  output [7:0] out_19
);

  wire fa_1_c, fa_2_c, fa_3_c, fa_4_c, fa_5_c, fa_6_c, fa_7_c, xor_1_out, xor_2_out, xor_3_out, xor_4_out,
       xor_5_out, xor_6_out, xor_7_out, xor_8_out;

  xor xor_1 (xor_1_out, Sel, Y0);
  xor xor_2 (xor_2_out, Sel, Y4);
  FA fa_1 (.X(X0), .Y(xor_1_out), .Z(Sel), .S(out_19[0]), .C(fa_1_c));
  FA fa_2 (.X(X4), .Y(xor_2_out), .Z(fa_7_c), .S(out_19[4]), .C(fa_2_c));
  xor xor_3 (xor_3_out, Sel, Y1);
  xor xor_4 (xor_4_out, Sel, Y5);
  FA fa_3 (.X(X1), .Y(xor_3_out), .Z(fa_1_c), .S(out_19[1]), .C(fa_3_c));
  FA fa_4 (.X(X5), .Y(xor_4_out), .Z(fa_2_c), .S(out_19[5]), .C(fa_4_c));
  xor xor_5 (xor_5_out, Sel, Y2);
  xor xor_6 (xor_6_out, Sel, Y6);
  FA fa_5 (.X(X2), .Y(xor_5_out), .Z(fa_3_c), .S(out_19[2]), .C(fa_5_c));
  FA fa_6 (.X(X6), .Y(xor_6_out), .Z(fa_4_c), .S(out_19[6]), .C(fa_6_c));
  xor xor_7 (xor_7_out, Sel, Y3);
  xor xor_8 (xor_8_out, Sel, Y7);
  FA fa_7 (.X(X3), .Y(xor_7_out), .Z(fa_5_c), .S(out_19[3]), .C(fa_7_c));
  FA fa_8 (.X(X7), .Y(xor_8_out), .Z(fa_6_c), .S(out_19[7]), .C(FC));
endmodule

module HA (
  input  X,
  input  Y,
  output S,
  output C
);

  xor xor_1 (S, X, Y);
  and and_1 (C, Y, X);
endmodule

module FA (
  input  X,
  input  Y,
  input  Z,
  output S,
  output C
);

  wire ha_1_c, ha_1_s, ha_2_c;

  HA ha_1 (.X(X), .Y(Y), .S(ha_1_s), .C(ha_1_c));
  HA ha_2 (.X(ha_1_s), .Y(Z), .S(S), .C(ha_2_c));
  or or_1 (C, ha_2_c, ha_1_c);
endmodule

module _8bitAddMod (
  input  [7:0] Dest,
  input  [7:0] Src,
  output X0,
  output [7:0] out_4
);

  A_S a_s_1 (
    .Sel(1'b0), .X0(Dest[0]), .X2(Dest[2]), .X3(Dest[3]), .X1(Dest[1]), .Y2(Src[2]), .Y3(Src[3]),
    .Y0(Src[0]), .Y1(Src[1]), .X7(Dest[7]), .X5(Dest[5]), .X6(Dest[6]), .X4(Dest[4]), .Y7(Src[7]),
    .Y5(Src[5]), .Y6(Src[6]), .Y4(Src[4]), .FC(out_4[7]), .out_19({out_4[6:0], X0}));
endmodule

module Mult (
  input  [7:0] Dest,
  input  [7:0] Src,
  output [7:0] out_3
);

  wire [7:0] mult_1_8_2_out_3, mult_1_8_3_out_3, mult_1_8_4_out_3, mult_1_8_5_out_3, mult_1_8_6_out_3,
       mult_1_8_7_out_3, mult_1_8_8_out_3, n8bitaddmod_1_out_4, n8bitaddmod_2_out_4, n8bitaddmod_3_out_4,
       n8bitaddmod_4_out_4, n8bitaddmod_5_out_4, n8bitaddmod_6_out_4, n8bitaddmod_7_out_4;
  wire [7:1] mult_1_8_1_out_3;

  Mult_1_8 mult_1_8_1 (.Dest(Dest), .X0(Src[0]), .out_3({mult_1_8_1_out_3, out_3[0]}));
  Mult_1_8 mult_1_8_2 (.Dest(Dest), .X0(Src[1]), .out_3(mult_1_8_2_out_3));
  Mult_1_8 mult_1_8_3 (.Dest(Dest), .X0(Src[2]), .out_3(mult_1_8_3_out_3));
  Mult_1_8 mult_1_8_4 (.Dest(Dest), .X0(Src[3]), .out_3(mult_1_8_4_out_3));
  Mult_1_8 mult_1_8_5 (.Dest(Dest), .X0(Src[4]), .out_3(mult_1_8_5_out_3));
  Mult_1_8 mult_1_8_6 (.Dest(Dest), .X0(Src[5]), .out_3(mult_1_8_6_out_3));
  Mult_1_8 mult_1_8_7 (.Dest(Dest), .X0(Src[6]), .out_3(mult_1_8_7_out_3));
  Mult_1_8 mult_1_8_8 (.Dest(Dest), .X0(Src[7]), .out_3(mult_1_8_8_out_3));
  _8bitAddMod u_8bitaddmod_1 (
    .Dest(n8bitaddmod_7_out_4), .Src(mult_1_8_3_out_3), .X0(out_3[2]), .out_4(n8bitaddmod_1_out_4));
  _8bitAddMod u_8bitaddmod_2 (
    .Dest(n8bitaddmod_1_out_4), .Src(mult_1_8_4_out_3), .X0(out_3[3]), .out_4(n8bitaddmod_2_out_4));
  _8bitAddMod u_8bitaddmod_3 (
    .Dest(n8bitaddmod_2_out_4), .Src(mult_1_8_5_out_3), .X0(out_3[4]), .out_4(n8bitaddmod_3_out_4));
  _8bitAddMod u_8bitaddmod_4 (
    .Dest(n8bitaddmod_3_out_4), .Src(mult_1_8_6_out_3), .X0(out_3[5]), .out_4(n8bitaddmod_4_out_4));
  _8bitAddMod u_8bitaddmod_5 (
    .Dest(n8bitaddmod_4_out_4), .Src(mult_1_8_7_out_3), .X0(out_3[6]), .out_4(n8bitaddmod_5_out_4));
  _8bitAddMod u_8bitaddmod_6 (
    .Dest(n8bitaddmod_5_out_4), .Src(mult_1_8_8_out_3), .X0(out_3[7]), .out_4(n8bitaddmod_6_out_4));
  _8bitAddMod u_8bitaddmod_7 (
    .Dest({1'b0, mult_1_8_1_out_3}), .Src(mult_1_8_2_out_3), .X0(out_3[1]), .out_4(n8bitaddmod_7_out_4));
endmodule

module Mult_1_8 (
  input  [7:0] Dest,
  input  X0,
  output [7:0] out_3
);

  and and_1 (out_3[0], Dest[0], X0);
  and and_2 (out_3[1], Dest[1], X0);
  and and_3 (out_3[2], Dest[2], X0);
  and and_4 (out_3[3], Dest[3], X0);
  and and_5 (out_3[4], Dest[4], X0);
  and and_6 (out_3[5], Dest[5], X0);
  and and_7 (out_3[6], Dest[6], X0);
  and and_8 (out_3[7], Dest[7], X0);
endmodule

module IMult (
  input  [7:0] Dest,
  input  [7:0] Src,
  output [7:0] out_3
);

  wire xor_1_out;
  wire [7:0] mult_1_out_3, n2_1mux_8bits_1_y, n2_1mux_8bits_2_y, neg_1_out_2, neg_2_out_2, neg_3_out_2;

  Neg neg_1 (.Dest(Src), .out_2(neg_1_out_2));
  Neg neg_2 (.Dest(Dest), .out_2(neg_2_out_2));
  _2_1Mux_8bits u_2_1mux_8bits_1 (.D0(Src), .D1(neg_1_out_2), .S0(Src[7]), .En(1'b1), .Y(n2_1mux_8bits_1_y));
  _2_1Mux_8bits u_2_1mux_8bits_2 (.D0(Dest), .D1(neg_2_out_2), .S0(Dest[7]), .En(1'b1), .Y(n2_1mux_8bits_2_y));
  Mult mult_1 (.Dest(n2_1mux_8bits_1_y), .Src(n2_1mux_8bits_2_y), .out_3(mult_1_out_3));
  xor xor_1 (xor_1_out, Dest[7], Src[7]);
  _2_1Mux_8bits u_2_1mux_8bits_3 (.D0(mult_1_out_3), .D1(neg_3_out_2), .S0(xor_1_out), .En(1'b1), .Y(out_3));
  Neg neg_3 (.Dest(mult_1_out_3), .out_2(neg_3_out_2));
endmodule

module Neg (
  input  [7:0] Dest,
  output [7:0] out_2
);

  wire or_1_out, or_2_out, or_3_out, or_4_out, or_5_out, or_6_out;

  or or_1 (or_1_out, Dest[5], or_6_out);
  or or_2 (or_2_out, Dest[6], or_1_out);
  or or_3 (or_3_out, Dest[1], Dest[0]);
  or or_4 (or_4_out, Dest[2], or_3_out);
  or or_5 (or_5_out, Dest[3], or_4_out);
  or or_6 (or_6_out, Dest[4], or_5_out);
  xor xor_1 (out_2[2], or_3_out, Dest[2]);
  xor xor_2 (out_2[3], Dest[3], or_4_out);
  xor xor_3 (out_2[4], Dest[4], or_5_out);
  xor xor_4 (out_2[5], Dest[5], or_6_out);
  xor xor_5 (out_2[6], Dest[6], or_1_out);
  xor xor_6 (out_2[7], Dest[7], or_2_out);
  xor xor_7 (out_2[1], Dest[0], Dest[1]);

  assign out_2[0] = Dest[0];
endmodule

module NOT (
  input  [7:0] Dest,
  output [7:0] out_2
);

  not not_1 (out_2[0], Dest[0]);
  not not_2 (out_2[1], Dest[1]);
  not not_3 (out_2[2], Dest[2]);
  not not_4 (out_2[3], Dest[3]);
  not not_5 (out_2[4], Dest[4]);
  not not_6 (out_2[5], Dest[5]);
  not not_7 (out_2[6], Dest[6]);
  not not_8 (out_2[7], Dest[7]);
endmodule

module AND (
  input  [7:0] Dest,
  input  [7:0] Src,
  output [7:0] out_3
);

  and and_1 (out_3[0], Src[0], Dest[0]);
  and and_2 (out_3[1], Src[1], Dest[1]);
  and and_3 (out_3[2], Src[2], Dest[2]);
  and and_4 (out_3[3], Src[3], Dest[3]);
  and and_5 (out_3[4], Src[4], Dest[4]);
  and and_6 (out_3[5], Src[5], Dest[5]);
  and and_7 (out_3[6], Src[6], Dest[6]);
  and and_8 (out_3[7], Src[7], Dest[7]);
endmodule

module OR (
  input  [7:0] Dest,
  input  [7:0] Src,
  output [7:0] out_3
);

  or or_1 (out_3[0], Src[0], Dest[0]);
  or or_2 (out_3[1], Src[1], Dest[1]);
  or or_3 (out_3[2], Src[2], Dest[2]);
  or or_4 (out_3[3], Src[3], Dest[3]);
  or or_5 (out_3[4], Src[4], Dest[4]);
  or or_6 (out_3[5], Src[5], Dest[5]);
  or or_7 (out_3[6], Src[6], Dest[6]);
  or or_8 (out_3[7], Src[7], Dest[7]);
endmodule

module XOR (
  input  [7:0] Dest,
  input  [7:0] Src,
  output [7:0] out_3
);

  xor xor_1 (out_3[0], Src[0], Dest[0]);
  xor xor_2 (out_3[1], Src[1], Dest[1]);
  xor xor_3 (out_3[2], Src[2], Dest[2]);
  xor xor_4 (out_3[3], Src[3], Dest[3]);
  xor xor_5 (out_3[4], Src[4], Dest[4]);
  xor xor_6 (out_3[5], Src[5], Dest[5]);
  xor xor_7 (out_3[6], Src[6], Dest[6]);
  xor xor_8 (out_3[7], Src[7], Dest[7]);
endmodule

module SHR (
  input  [7:0] Dest,
  input  [7:0] Src,
  output [7:0] out_3
);

  wire not_1_out, or_1_out;
  wire [7:0] n8_1mux_1_y, sh1_1_out_3, sh1_2_out_3, sh1_3_out_3, sh1_4_out_3, sh1_5_out_3, sh1_6_out_3,
       sh1_7_out_3;

  SH1 sh1_1 (.Dest(Dest), .Selc(1'b1), .out_3(sh1_1_out_3));
  SH1 sh1_2 (.Dest(sh1_1_out_3), .Selc(1'b1), .out_3(sh1_2_out_3));
  SH1 sh1_3 (.Dest(sh1_2_out_3), .Selc(1'b1), .out_3(sh1_3_out_3));
  or or_1 (or_1_out, Src[3], Src[4], Src[5], Src[6], Src[7]);
  SH1 sh1_4 (.Dest(sh1_3_out_3), .Selc(1'b1), .out_3(sh1_4_out_3));
  SH1 sh1_5 (.Dest(sh1_4_out_3), .Selc(1'b1), .out_3(sh1_5_out_3));
  SH1 sh1_6 (.Dest(sh1_5_out_3), .Selc(1'b1), .out_3(sh1_6_out_3));
  SH1 sh1_7 (.Dest(sh1_6_out_3), .Selc(1'b1), .out_3(sh1_7_out_3));
  _8_1Mux u_8_1mux_1 (
    .D0(Dest), .D1(sh1_1_out_3), .D2(sh1_2_out_3), .D3(sh1_3_out_3), .S(Src[2:0]), .D4(sh1_4_out_3),
    .D5(sh1_5_out_3), .D6(sh1_6_out_3), .D7(sh1_7_out_3), .Y(n8_1mux_1_y), .En(1'b1));
  not not_1 (not_1_out, or_1_out);
  _2_1Mux_8bits u_2_1mux_8bits_1 (.D0({8{1'b0}}), .D1(n8_1mux_1_y), .S0(not_1_out), .En(1'b1), .Y(out_3));
endmodule

module SHL (
  input  [7:0] Dest,
  input  [7:0] Src,
  output [7:0] out_3
);

  wire not_1_out, not_2_out, or_1_out;
  wire [7:0] n8_1mux_1_y, sh1_1_out_3, sh1_2_out_3, sh1_3_out_3, sh1_4_out_3, sh1_5_out_3, sh1_6_out_3,
       sh1_7_out_3;

  SH1 sh1_1 (.Dest(Dest), .Selc(1'b0), .out_3(sh1_1_out_3));
  SH1 sh1_2 (.Dest(sh1_1_out_3), .Selc(1'b0), .out_3(sh1_2_out_3));
  SH1 sh1_3 (.Dest(sh1_2_out_3), .Selc(1'b0), .out_3(sh1_3_out_3));
  or or_1 (or_1_out, Src[3], Src[4], Src[5], Src[6], Src[7]);
  SH1 sh1_4 (.Dest(sh1_3_out_3), .Selc(1'b0), .out_3(sh1_4_out_3));
  SH1 sh1_5 (.Dest(sh1_4_out_3), .Selc(1'b0), .out_3(sh1_5_out_3));
  SH1 sh1_6 (.Dest(sh1_5_out_3), .Selc(1'b0), .out_3(sh1_6_out_3));
  SH1 sh1_7 (.Dest(sh1_6_out_3), .Selc(1'b0), .out_3(sh1_7_out_3));
  not not_1 (not_1_out, or_1_out);
  not not_2 (not_2_out, 1'b0);
  _8_1Mux u_8_1mux_1 (
    .D0(Dest), .D1(sh1_1_out_3), .D2(sh1_2_out_3), .D3(sh1_3_out_3), .S(Src[2:0]), .D4(sh1_4_out_3),
    .D5(sh1_5_out_3), .D6(sh1_6_out_3), .D7(sh1_7_out_3), .Y(n8_1mux_1_y), .En(not_2_out));
  _2_1Mux_8bits u_2_1mux_8bits_1 (.D0({8{1'b0}}), .D1(n8_1mux_1_y), .S0(not_1_out), .En(not_2_out), .Y(out_3));
endmodule

module SH1 (
  input  [7:0] Dest,
  input  Selc,
  output [7:0] out_3
);

  _2_1Mux_8bits u_2_1mux_8bits_1 (.D0({Dest[6:0], 1'b0}), .D1({1'b0, Dest[7:1]}), .S0(Selc), .En(1'b1), .Y(out_3));
endmodule

module _2_1Mux_1bit (
  input  S0,
  input  D0,
  input  D1,
  input  En,
  output Y
);

  wire and_1_out, and_2_out, not_1_out, or_1_out;

  not not_1 (not_1_out, S0);
  and and_1 (and_1_out, not_1_out, D0);
  and and_2 (and_2_out, S0, D1);
  or or_1 (or_1_out, and_1_out, and_2_out);
  and and_3 (Y, or_1_out, En);
endmodule

module _2_1Mux_8bits (
  input  [7:0] D0,
  input  [7:0] D1,
  input  S0,
  input  En,
  output [7:0] Y
);

  _2_1Mux_1bit u_2_1mux_1bit_1 (.S0(S0), .D0(D0[7]), .D1(D1[7]), .En(En), .Y(Y[7]));
  _2_1Mux_1bit u_2_1mux_1bit_2 (.S0(S0), .D0(D0[6]), .D1(D1[6]), .En(En), .Y(Y[6]));
  _2_1Mux_1bit u_2_1mux_1bit_3 (.S0(S0), .D0(D0[5]), .D1(D1[5]), .En(En), .Y(Y[5]));
  _2_1Mux_1bit u_2_1mux_1bit_4 (.S0(S0), .D0(D0[4]), .D1(D1[4]), .En(En), .Y(Y[4]));
  _2_1Mux_1bit u_2_1mux_1bit_5 (.S0(S0), .D0(D0[3]), .D1(D1[3]), .En(En), .Y(Y[3]));
  _2_1Mux_1bit u_2_1mux_1bit_6 (.S0(S0), .D0(D0[2]), .D1(D1[2]), .En(En), .Y(Y[2]));
  _2_1Mux_1bit u_2_1mux_1bit_7 (.S0(S0), .D0(D0[1]), .D1(D1[1]), .En(En), .Y(Y[1]));
  _2_1Mux_1bit u_2_1mux_1bit_8 (.S0(S0), .D0(D0[0]), .D1(D1[0]), .En(En), .Y(Y[0]));
endmodule

module _4_1Mux (
  input  [7:0] D0,
  input  [7:0] D1,
  input  [7:0] D2,
  input  [7:0] D3,
  input  En,
  input  [1:0] S,
  output [7:0] Y
);

  wire and_1_out, and_2_out, not_1_out;
  wire [7:0] n2_1mux_8bits_1_y, n2_1mux_8bits_2_y;

  not not_1 (not_1_out, S[1]);
  and and_1 (and_1_out, not_1_out, En);
  and and_2 (and_2_out, S[1], En);
  _2_1Mux_8bits u_2_1mux_8bits_1 (.D0(D0), .D1(D1), .S0(S[0]), .En(and_1_out), .Y(n2_1mux_8bits_1_y));
  _2_1Mux_8bits u_2_1mux_8bits_2 (.D0(D2), .D1(D3), .S0(S[0]), .En(and_2_out), .Y(n2_1mux_8bits_2_y));
  _2_1Mux_8bits u_2_1mux_8bits_3 (.D0(n2_1mux_8bits_1_y), .D1(n2_1mux_8bits_2_y), .S0(S[1]), .En(En), .Y(Y));
endmodule

module _8_1Mux (
  input  [7:0] D0,
  input  [7:0] D1,
  input  [7:0] D2,
  input  [7:0] D3,
  input  [2:0] S,
  input  En,
  input  [7:0] D4,
  input  [7:0] D5,
  input  [7:0] D6,
  input  [7:0] D7,
  output [7:0] Y
);

  wire and_1_out, and_2_out, not_1_out;
  wire [7:0] n4_1mux_1_y, n4_1mux_2_y;

  not not_1 (not_1_out, S[2]);
  and and_1 (and_1_out, S[2], En);
  and and_2 (and_2_out, not_1_out, En);
  _4_1Mux u_4_1mux_1 (.D0(D0), .D1(D1), .D2(D2), .D3(D3), .En(and_2_out), .S(S[1:0]), .Y(n4_1mux_1_y));
  _4_1Mux u_4_1mux_2 (.D0(D4), .D1(D5), .D2(D6), .D3(D7), .En(and_1_out), .S(S[1:0]), .Y(n4_1mux_2_y));
  _2_1Mux_8bits u_2_1mux_8bits_1 (.D0(n4_1mux_1_y), .D1(n4_1mux_2_y), .S0(S[2]), .En(En), .Y(Y));
endmodule

module _16_1Mux (
  input  [7:0] D8,
  input  [7:0] D0,
  input  [7:0] D9,
  input  [7:0] D1,
  input  [7:0] D10,
  input  [7:0] D2,
  input  [7:0] D11,
  input  [7:0] D3,
  input  [7:0] D12,
  input  [7:0] D4,
  input  [7:0] D13,
  input  [7:0] D5,
  input  [7:0] D14,
  input  [7:0] D6,
  input  [7:0] D15,
  input  [7:0] D7,
  input  [3:0] S,
  input  En,
  output [7:0] out_19
);

  wire and_1_out, and_2_out, not_1_out;
  wire [7:0] n8_1mux_1_y, n8_1mux_2_y;

  not not_1 (not_1_out, S[3]);
  and and_1 (and_1_out, not_1_out, En);
  and and_2 (and_2_out, S[3], En);
  _8_1Mux u_8_1mux_1 (
    .D0(D0), .D1(D1), .D2(D2), .D3(D3), .S(S[2:0]), .D4(D4), .D5(D5), .D6(D6), .D7(D7), .Y(n8_1mux_1_y),
    .En(and_1_out));
  _8_1Mux u_8_1mux_2 (
    .D0(D8), .D1(D9), .D2(D10), .D3(D11), .S(S[2:0]), .D4(D12), .D5(D13), .D6(D14), .D7(D15),
    .Y(n8_1mux_2_y), .En(and_2_out));
  _2_1Mux_8bits u_2_1mux_8bits_1 (.D0(n8_1mux_1_y), .D1(n8_1mux_2_y), .S0(S[3]), .En(En), .Y(out_19));
endmodule

module _32_1Mux (
  input  [7:0] D0,
  input  [7:0] D1,
  input  [7:0] D2,
  input  [7:0] D3,
  input  [7:0] D4,
  input  [7:0] D5,
  input  [7:0] D6,
  input  [7:0] D7,
  input  [7:0] D8,
  input  [7:0] D9,
  input  [7:0] D10,
  input  [7:0] D11,
  input  [7:0] D12,
  input  [7:0] D13,
  input  [7:0] D14,
  input  [7:0] D15,
  input  [4:0] S,
  input  [7:0] D16,
  input  [7:0] D17,
  input  [7:0] D18,
  input  [7:0] D19,
  input  [7:0] D20,
  input  [7:0] D21,
  input  [7:0] D22,
  input  [7:0] D23,
  input  [7:0] D24,
  input  [7:0] D25,
  input  [7:0] D26,
  input  [7:0] D27,
  input  [7:0] D28,
  input  [7:0] D29,
  input  [7:0] D30,
  input  [7:0] D31,
  output [7:0] Y
);

  wire not_1_out;
  wire [7:0] n16_1mux_1_out_19, n16_1mux_2_out_19;

  _16_1Mux u_16_1mux_1 (
    .D8(D8), .D0(D0), .D9(D9), .D1(D1), .D10(D10), .D2(D2), .D11(D11), .D3(D3), .D12(D12), .D4(D4),
    .D13(D13), .D5(D5), .D14(D14), .D6(D6), .D15(D15), .D7(D7), .S(S[3:0]), .En(not_1_out),
    .out_19(n16_1mux_1_out_19));
  not not_1 (not_1_out, S[4]);
  _16_1Mux u_16_1mux_2 (
    .D8(D24), .D0(D16), .D9(D25), .D1(D17), .D10(D26), .D2(D18), .D11(D27), .D3(D19), .D12(D28), .D4(D20),
    .D13(D29), .D5(D21), .D14(D30), .D6(D22), .D15(D31), .D7(D23), .S(S[3:0]), .En(S[4]),
    .out_19(n16_1mux_2_out_19));
  _2_1Mux_8bits u_2_1mux_8bits_1 (.D0(n16_1mux_1_out_19), .D1(n16_1mux_2_out_19), .S0(S[4]), .En(1'b1), .Y(Y));
endmodule

module _2_4Dec (
  input  [1:0] in_1,
  output D0,
  output D1,
  output D2,
  output D3
);

  wire not_1_out, not_2_out;

  not not_1 (not_1_out, in_1[0]);
  not not_2 (not_2_out, in_1[1]);
  and and_1 (D0, not_1_out, not_2_out);
  and and_2 (D1, in_1[0], not_2_out);
  and and_3 (D2, not_1_out, in_1[1]);
  and and_4 (D3, in_1[1], in_1[0]);
endmodule
